// Logisim project 32-Single_Cycle_CPU_MD.Muntasir_Ahmed_1921333042_Sec_7.circ as structural Verilog
module _1_bit_Logic_unit (
  input  A,
  input  B,
  input  [2:0] S1S0,
  output Result
);

  wire nand_1_out, nor_1_out, xor_1_out;

  nand nand_1 (nand_1_out, A, B);
  nor nor_1 (nor_1_out, A, B);
  xor xor_1 (xor_1_out, A, B);
  Multiplexer #(.select(3), .enable("false")) multiplexer_1 (
    .in0(1'b0), .in1(1'b0), .in2(1'b0), .in3(nand_1_out), .in4(nor_1_out), .in5(xor_1_out), .in6(1'b0),
    .in7(1'b0), .out(Result), .sel(S1S0));
endmodule

module _4_bit_LU (
  input  [3:0] A,
  input  [3:0] B,
  input  [2:0] S1S0,
  output [3:0] Result
);

  _1_bit_Logic_unit u_1_bit_logic_unit_1 (.A(A[0]), .B(B[0]), .S1S0(S1S0), .Result(Result[0]));
  _1_bit_Logic_unit u_1_bit_logic_unit_2 (.A(A[1]), .B(B[1]), .S1S0(S1S0), .Result(Result[1]));
  _1_bit_Logic_unit u_1_bit_logic_unit_3 (.A(A[2]), .B(B[2]), .S1S0(S1S0), .Result(Result[2]));
  _1_bit_Logic_unit u_1_bit_logic_unit_4 (.A(A[3]), .B(B[3]), .S1S0(S1S0), .Result(Result[3]));
endmodule

module _1_bit_Adder (
  input  A,
  input  B,
  input  Cin,
  output S,
  output Cout
);

  wire and_1_out, and_2_out, xor_1_out;

  xor xor_1 (xor_1_out, A, B);
  and and_1 (and_1_out, Cin, xor_1_out);
  and and_2 (and_2_out, B, A);
  xor xor_2 (S, xor_1_out, Cin);
  or or_1 (Cout, and_1_out, and_2_out);
endmodule

module _1_bit_Arithmetic_Unit (
  input  Cin,
  input  A,
  input  B,
  input  [2:0] S2S1S0,
  output Sum,
  output Count
);

  wire multiplexer_1_out, not_1_out;

  not not_1 (not_1_out, B);
  Multiplexer #(.select(3), .enable("false")) multiplexer_1 (
    .in0(1'b0), .in1(1'b0), .in2(B), .in3(1'b0), .in4(1'b0), .in5(1'b0), .in6(not_1_out), .in7(1'b0),
    .out(multiplexer_1_out), .sel(S2S1S0));
  _1_bit_Adder u_1_bit_adder_1 (.A(A), .B(multiplexer_1_out), .Cin(Cin), .S(Sum), .Cout(Count));
endmodule

module _4_bit_Arithmetic_Unit (
  input  A3,
  input  A2,
  input  A1,
  input  A0,
  input  B3,
  input  B2,
  input  B1,
  input  B0,
  input  [2:0] S2S1S0,
  input  Cin,
  output Cout,
  output S3,
  output S2,
  output S1,
  output S0
);

  wire n1_bit_arithmetic_unit_1_count, n1_bit_arithmetic_unit_2_count, n1_bit_arithmetic_unit_3_count;

  _1_bit_Arithmetic_Unit u_1_bit_arithmetic_unit_1 (
    .Cin(Cin), .A(A0), .B(B0), .S2S1S0(S2S1S0), .Sum(S0), .Count(n1_bit_arithmetic_unit_1_count));
  _1_bit_Arithmetic_Unit u_1_bit_arithmetic_unit_2 (
    .Cin(n1_bit_arithmetic_unit_1_count), .A(A1), .B(B1), .S2S1S0(S2S1S0), .Sum(S1),
    .Count(n1_bit_arithmetic_unit_2_count));
  _1_bit_Arithmetic_Unit u_1_bit_arithmetic_unit_3 (
    .Cin(n1_bit_arithmetic_unit_2_count), .A(A2), .B(B2), .S2S1S0(S2S1S0), .Sum(S2),
    .Count(n1_bit_arithmetic_unit_3_count));
  _1_bit_Arithmetic_Unit u_1_bit_arithmetic_unit_4 (
    .Cin(n1_bit_arithmetic_unit_3_count), .A(A3), .B(B3), .S2S1S0(S2S1S0), .Sum(S3), .Count(Cout));
endmodule

module _32_bit_LU (
  input  [31:0] A,
  input  [31:0] B,
  input  [2:0] S1S0,
  output [31:0] Output
);

  _4_bit_LU u_4_bit_lu_1 (.S1S0(S1S0), .A(A[3:0]), .B(B[3:0]), .Result(Output[3:0]));
  _4_bit_LU u_4_bit_lu_2 (.S1S0(S1S0), .A(A[7:4]), .B(B[7:4]), .Result(Output[7:4]));
  _4_bit_LU u_4_bit_lu_3 (.S1S0(S1S0), .A(A[11:8]), .B(B[11:8]), .Result(Output[11:8]));
  _4_bit_LU u_4_bit_lu_4 (.S1S0(S1S0), .A(A[15:12]), .B(B[15:12]), .Result(Output[15:12]));
  _4_bit_LU u_4_bit_lu_5 (.S1S0(S1S0), .A(A[19:16]), .B(B[19:16]), .Result(Output[19:16]));
  _4_bit_LU u_4_bit_lu_6 (.S1S0(S1S0), .A(A[23:20]), .B(B[23:20]), .Result(Output[23:20]));
  _4_bit_LU u_4_bit_lu_7 (.S1S0(S1S0), .A(A[27:24]), .B(B[27:24]), .Result(Output[27:24]));
  _4_bit_LU u_4_bit_lu_8 (.S1S0(S1S0), .A(A[31:28]), .B(B[31:28]), .Result(Output[31:28]));
endmodule

module _32_bit_Arithmetic_Unit (
  input  [31:0] A,
  input  [31:0] B,
  input  [2:0] S2S1S0,
  input  Cin,
  output Cout,
  output [31:0] Output
);

  wire n4_bit_arithmetic_unit_1_cout, n4_bit_arithmetic_unit_2_cout, n4_bit_arithmetic_unit_3_cout,
       n4_bit_arithmetic_unit_4_cout, n4_bit_arithmetic_unit_5_cout, n4_bit_arithmetic_unit_6_cout,
       n4_bit_arithmetic_unit_7_cout;

  // Probe on A
  // Probe on B
  _4_bit_Arithmetic_Unit u_4_bit_arithmetic_unit_1 (
    .Cin(Cin), .S2S1S0(S2S1S0), .Cout(n4_bit_arithmetic_unit_1_cout), .A3(A[3]), .A2(A[2]), .A1(A[1]),
    .A0(A[0]), .B3(B[3]), .B2(B[2]), .B1(B[1]), .B0(B[0]), .S3(Output[3]), .S2(Output[2]), .S1(Output[1]),
    .S0(Output[0]));
  _4_bit_Arithmetic_Unit u_4_bit_arithmetic_unit_2 (
    .Cin(n4_bit_arithmetic_unit_1_cout), .S2S1S0(S2S1S0), .Cout(n4_bit_arithmetic_unit_2_cout), .A3(A[7]),
    .A2(A[6]), .A1(A[5]), .A0(A[4]), .B3(B[7]), .B2(B[6]), .B1(B[5]), .B0(B[4]), .S3(Output[7]),
    .S2(Output[6]), .S1(Output[5]), .S0(Output[4]));
  _4_bit_Arithmetic_Unit u_4_bit_arithmetic_unit_3 (
    .Cin(n4_bit_arithmetic_unit_2_cout), .S2S1S0(S2S1S0), .Cout(n4_bit_arithmetic_unit_3_cout), .A3(A[11]),
    .A2(A[10]), .A1(A[9]), .A0(A[8]), .B3(B[11]), .B2(B[10]), .B1(B[9]), .B0(B[8]), .S3(Output[11]),
    .S2(Output[10]), .S1(Output[9]), .S0(Output[8]));
  _4_bit_Arithmetic_Unit u_4_bit_arithmetic_unit_4 (
    .Cin(n4_bit_arithmetic_unit_3_cout), .S2S1S0(S2S1S0), .Cout(n4_bit_arithmetic_unit_4_cout), .A3(A[15]),
    .A2(A[14]), .A1(A[13]), .A0(A[12]), .B3(B[15]), .B2(B[14]), .B1(B[13]), .B0(B[12]), .S3(Output[15]),
    .S2(Output[14]), .S1(Output[13]), .S0(Output[12]));
  _4_bit_Arithmetic_Unit u_4_bit_arithmetic_unit_5 (
    .Cin(n4_bit_arithmetic_unit_4_cout), .S2S1S0(S2S1S0), .Cout(n4_bit_arithmetic_unit_5_cout), .A3(A[19]),
    .A2(A[18]), .A1(A[17]), .A0(A[16]), .B3(B[19]), .B2(B[18]), .B1(B[17]), .B0(B[16]), .S3(Output[19]),
    .S2(Output[18]), .S1(Output[17]), .S0(Output[16]));
  _4_bit_Arithmetic_Unit u_4_bit_arithmetic_unit_6 (
    .Cin(n4_bit_arithmetic_unit_5_cout), .S2S1S0(S2S1S0), .Cout(n4_bit_arithmetic_unit_6_cout), .A3(A[23]),
    .A2(A[22]), .A1(A[21]), .A0(A[20]), .B3(B[23]), .B2(B[22]), .B1(B[21]), .B0(B[20]), .S3(Output[23]),
    .S2(Output[22]), .S1(Output[21]), .S0(Output[20]));
  _4_bit_Arithmetic_Unit u_4_bit_arithmetic_unit_7 (
    .Cin(n4_bit_arithmetic_unit_6_cout), .S2S1S0(S2S1S0), .Cout(n4_bit_arithmetic_unit_7_cout), .A3(A[27]),
    .A2(A[26]), .A1(A[25]), .A0(A[24]), .B3(B[27]), .B2(B[26]), .B1(B[25]), .B0(B[24]), .S3(Output[27]),
    .S2(Output[26]), .S1(Output[25]), .S0(Output[24]));
  _4_bit_Arithmetic_Unit u_4_bit_arithmetic_unit_8 (
    .Cin(n4_bit_arithmetic_unit_7_cout), .S2S1S0(S2S1S0), .Cout(Cout), .A3(A[31]), .A2(A[30]), .A1(A[29]),
    .A0(A[28]), .B3(B[31]), .B2(B[30]), .B1(B[29]), .B0(B[28]), .S3(Output[31]), .S2(Output[30]),
    .S1(Output[29]), .S0(Output[28]));
  // Probe on Output
endmodule

module _16_bit_Adder (
  input  A15,
  input  A14,
  input  A13,
  input  A12,
  input  A11,
  input  A10,
  input  A9,
  input  A8,
  input  A7,
  input  A6,
  input  A5,
  input  A4,
  input  A3,
  input  A2,
  input  A1,
  input  A0,
  input  B15,
  input  B14,
  input  B13,
  input  B12,
  input  B11,
  input  B10,
  input  B9,
  input  B8,
  input  B7,
  input  B6,
  input  B5,
  input  B4,
  input  B3,
  input  B2,
  input  B1,
  input  B0,
  input  Cin,
  output S15,
  output S14,
  output S13,
  output S12,
  output S11,
  output S10,
  output S9,
  output S8,
  output S7,
  output S6,
  output S5,
  output S4,
  output S3,
  output S2,
  output S1,
  output S0,
  output Cout
);

  wire n1_bit_adder_1_cout, n1_bit_adder_2_cout, n1_bit_adder_3_cout, n1_bit_adder_4_cout,
       n1_bit_adder_5_cout, n1_bit_adder_6_cout, n1_bit_adder_7_cout, n1_bit_adder_8_cout,
       n1_bit_adder_9_cout, n1_bit_adder_10_cout, n1_bit_adder_11_cout, n1_bit_adder_12_cout,
       n1_bit_adder_13_cout, n1_bit_adder_14_cout, n1_bit_adder_15_cout;

  _1_bit_Adder u_1_bit_adder_1 (.A(A0), .B(B0), .Cin(Cin), .S(S0), .Cout(n1_bit_adder_1_cout));
  _1_bit_Adder u_1_bit_adder_2 (.A(A1), .B(B1), .Cin(n1_bit_adder_1_cout), .S(S1), .Cout(n1_bit_adder_2_cout));
  _1_bit_Adder u_1_bit_adder_3 (.A(A2), .B(B2), .Cin(n1_bit_adder_2_cout), .S(S2), .Cout(n1_bit_adder_3_cout));
  _1_bit_Adder u_1_bit_adder_4 (.A(A3), .B(B3), .Cin(n1_bit_adder_3_cout), .S(S3), .Cout(n1_bit_adder_4_cout));
  _1_bit_Adder u_1_bit_adder_5 (.A(A4), .B(B4), .Cin(n1_bit_adder_4_cout), .S(S4), .Cout(n1_bit_adder_5_cout));
  _1_bit_Adder u_1_bit_adder_6 (.A(A5), .B(B5), .Cin(n1_bit_adder_5_cout), .S(S5), .Cout(n1_bit_adder_6_cout));
  _1_bit_Adder u_1_bit_adder_7 (.A(A6), .B(B6), .Cin(n1_bit_adder_6_cout), .S(S6), .Cout(n1_bit_adder_7_cout));
  _1_bit_Adder u_1_bit_adder_8 (.A(A7), .B(B7), .Cin(n1_bit_adder_7_cout), .S(S7), .Cout(n1_bit_adder_8_cout));
  _1_bit_Adder u_1_bit_adder_9 (.A(A8), .B(B8), .Cin(n1_bit_adder_8_cout), .S(S8), .Cout(n1_bit_adder_9_cout));
  _1_bit_Adder u_1_bit_adder_10 (.A(A9), .B(B9), .Cin(n1_bit_adder_9_cout), .S(S9), .Cout(n1_bit_adder_10_cout));
  _1_bit_Adder u_1_bit_adder_11 (.A(A10), .B(B10), .Cin(n1_bit_adder_10_cout), .S(S10), .Cout(n1_bit_adder_11_cout));
  _1_bit_Adder u_1_bit_adder_12 (.A(A11), .B(B11), .Cin(n1_bit_adder_11_cout), .S(S11), .Cout(n1_bit_adder_12_cout));
  _1_bit_Adder u_1_bit_adder_13 (.A(A12), .B(B12), .Cin(n1_bit_adder_12_cout), .S(S12), .Cout(n1_bit_adder_13_cout));
  _1_bit_Adder u_1_bit_adder_14 (.A(A13), .B(B13), .Cin(n1_bit_adder_13_cout), .S(S13), .Cout(n1_bit_adder_14_cout));
  _1_bit_Adder u_1_bit_adder_15 (.A(A14), .B(B14), .Cin(n1_bit_adder_14_cout), .S(S14), .Cout(n1_bit_adder_15_cout));
  _1_bit_Adder u_1_bit_adder_16 (.A(A15), .B(B15), .Cin(n1_bit_adder_15_cout), .S(S15), .Cout(Cout));
endmodule

module _16x16_Multiplier (
  input  [15:0] A,
  input  [15:0] B,
  output [31:0] Output
);

  wire and_2_out, and_3_out, and_4_out, and_5_out, and_6_out, and_7_out, and_8_out, and_9_out, and_10_out,
       and_11_out, and_12_out, and_13_out, and_14_out, and_15_out, and_16_out, and_17_out, and_18_out,
       and_19_out, and_20_out, and_21_out, and_22_out, and_23_out, and_24_out, and_25_out, and_26_out,
       and_27_out, and_28_out, and_29_out, and_30_out, and_31_out, and_32_out, and_33_out, and_34_out,
       and_35_out, and_36_out, and_37_out, and_38_out, and_39_out, and_40_out, and_41_out, and_42_out,
       and_43_out, and_44_out, and_45_out, and_46_out, and_47_out, and_48_out, and_49_out, and_50_out,
       and_51_out, and_52_out, and_53_out, and_54_out, and_55_out, and_56_out, and_57_out, and_58_out,
       and_59_out, and_60_out, and_61_out, and_62_out, and_63_out, and_64_out, and_65_out, and_66_out,
       and_67_out, and_68_out, and_69_out, and_70_out, and_71_out, and_72_out, and_73_out, and_74_out,
       and_75_out, and_76_out, and_77_out, and_78_out, and_79_out, and_80_out, and_81_out, and_82_out,
       and_83_out, and_84_out, and_85_out, and_86_out, and_87_out, and_88_out, and_89_out, and_90_out,
       and_91_out, and_92_out, and_93_out, and_94_out, and_95_out, and_96_out, and_97_out, and_98_out,
       and_99_out, and_100_out, and_101_out, and_102_out, and_103_out, and_104_out, and_105_out, and_106_out,
       and_107_out, and_108_out, and_109_out, and_110_out, and_111_out, and_112_out, and_113_out,
       and_114_out, and_115_out, and_116_out, and_117_out, and_118_out, and_119_out, and_120_out,
       and_121_out, and_122_out, and_123_out, and_124_out, and_125_out, and_126_out, and_127_out,
       and_128_out, and_129_out, and_130_out, and_131_out, and_132_out, and_133_out, and_134_out,
       and_135_out, and_136_out, and_137_out, and_138_out, and_139_out, and_140_out, and_141_out,
       and_142_out, and_143_out, and_144_out, and_145_out, and_146_out, and_147_out, and_148_out,
       and_149_out, and_150_out, and_151_out, and_152_out, and_153_out, and_154_out, and_155_out,
       and_156_out, and_157_out, and_158_out, and_159_out, and_160_out, and_161_out, and_162_out,
       and_163_out, and_164_out, and_165_out, and_166_out, and_167_out, and_168_out, and_169_out,
       and_170_out, and_171_out, and_172_out, and_173_out, and_174_out, and_175_out, and_176_out,
       and_177_out, and_178_out, and_179_out, and_180_out, and_181_out, and_182_out, and_183_out,
       and_184_out, and_185_out, and_186_out, and_187_out, and_188_out, and_189_out, and_190_out,
       and_191_out, and_192_out, and_193_out, and_194_out, and_195_out, and_196_out, and_197_out,
       and_198_out, and_199_out, and_200_out, and_201_out, and_202_out, and_203_out, and_204_out,
       and_205_out, and_206_out, and_207_out, and_208_out, and_209_out, and_210_out, and_211_out,
       and_212_out, and_213_out, and_214_out, and_215_out, and_216_out, and_217_out, and_218_out,
       and_219_out, and_220_out, and_221_out, and_222_out, and_223_out, and_224_out, and_225_out,
       and_226_out, and_227_out, and_228_out, and_229_out, and_230_out, and_231_out, and_232_out,
       and_233_out, and_234_out, and_235_out, and_236_out, and_237_out, and_238_out, and_239_out,
       and_240_out, and_241_out, and_242_out, and_243_out, and_244_out, and_245_out, and_246_out,
       and_247_out, and_248_out, and_249_out, and_250_out, and_251_out, and_252_out, and_253_out,
       and_254_out, and_255_out, and_256_out, n16_bit_adder_1_cout, n16_bit_adder_1_s1, n16_bit_adder_1_s2,
       n16_bit_adder_1_s3, n16_bit_adder_1_s4, n16_bit_adder_1_s5, n16_bit_adder_1_s6, n16_bit_adder_1_s7,
       n16_bit_adder_1_s8, n16_bit_adder_1_s9, n16_bit_adder_1_s10, n16_bit_adder_1_s11, n16_bit_adder_1_s12,
       n16_bit_adder_1_s13, n16_bit_adder_1_s14, n16_bit_adder_1_s15, n16_bit_adder_2_cout,
       n16_bit_adder_2_s1, n16_bit_adder_2_s2, n16_bit_adder_2_s3, n16_bit_adder_2_s4, n16_bit_adder_2_s5,
       n16_bit_adder_2_s6, n16_bit_adder_2_s7, n16_bit_adder_2_s8, n16_bit_adder_2_s9, n16_bit_adder_2_s10,
       n16_bit_adder_2_s11, n16_bit_adder_2_s12, n16_bit_adder_2_s13, n16_bit_adder_2_s14,
       n16_bit_adder_2_s15, n16_bit_adder_3_cout, n16_bit_adder_3_s1, n16_bit_adder_3_s2, n16_bit_adder_3_s3,
       n16_bit_adder_3_s4, n16_bit_adder_3_s5, n16_bit_adder_3_s6, n16_bit_adder_3_s7, n16_bit_adder_3_s8,
       n16_bit_adder_3_s9, n16_bit_adder_3_s10, n16_bit_adder_3_s11, n16_bit_adder_3_s12,
       n16_bit_adder_3_s13, n16_bit_adder_3_s14, n16_bit_adder_3_s15, n16_bit_adder_4_cout,
       n16_bit_adder_4_s1, n16_bit_adder_4_s2, n16_bit_adder_4_s3, n16_bit_adder_4_s4, n16_bit_adder_4_s5,
       n16_bit_adder_4_s6, n16_bit_adder_4_s7, n16_bit_adder_4_s8, n16_bit_adder_4_s9, n16_bit_adder_4_s10,
       n16_bit_adder_4_s11, n16_bit_adder_4_s12, n16_bit_adder_4_s13, n16_bit_adder_4_s14,
       n16_bit_adder_4_s15, n16_bit_adder_5_cout, n16_bit_adder_5_s1, n16_bit_adder_5_s2, n16_bit_adder_5_s3,
       n16_bit_adder_5_s4, n16_bit_adder_5_s5, n16_bit_adder_5_s6, n16_bit_adder_5_s7, n16_bit_adder_5_s8,
       n16_bit_adder_5_s9, n16_bit_adder_5_s10, n16_bit_adder_5_s11, n16_bit_adder_5_s12,
       n16_bit_adder_5_s13, n16_bit_adder_5_s14, n16_bit_adder_5_s15, n16_bit_adder_6_cout,
       n16_bit_adder_6_s1, n16_bit_adder_6_s2, n16_bit_adder_6_s3, n16_bit_adder_6_s4, n16_bit_adder_6_s5,
       n16_bit_adder_6_s6, n16_bit_adder_6_s7, n16_bit_adder_6_s8, n16_bit_adder_6_s9, n16_bit_adder_6_s10,
       n16_bit_adder_6_s11, n16_bit_adder_6_s12, n16_bit_adder_6_s13, n16_bit_adder_6_s14,
       n16_bit_adder_6_s15, n16_bit_adder_7_cout, n16_bit_adder_7_s1, n16_bit_adder_7_s2, n16_bit_adder_7_s3,
       n16_bit_adder_7_s4, n16_bit_adder_7_s5, n16_bit_adder_7_s6, n16_bit_adder_7_s7, n16_bit_adder_7_s8,
       n16_bit_adder_7_s9, n16_bit_adder_7_s10, n16_bit_adder_7_s11, n16_bit_adder_7_s12,
       n16_bit_adder_7_s13, n16_bit_adder_7_s14, n16_bit_adder_7_s15, n16_bit_adder_8_cout,
       n16_bit_adder_8_s1, n16_bit_adder_8_s2, n16_bit_adder_8_s3, n16_bit_adder_8_s4, n16_bit_adder_8_s5,
       n16_bit_adder_8_s6, n16_bit_adder_8_s7, n16_bit_adder_8_s8, n16_bit_adder_8_s9, n16_bit_adder_8_s10,
       n16_bit_adder_8_s11, n16_bit_adder_8_s12, n16_bit_adder_8_s13, n16_bit_adder_8_s14,
       n16_bit_adder_8_s15, n16_bit_adder_9_cout, n16_bit_adder_9_s1, n16_bit_adder_9_s2, n16_bit_adder_9_s3,
       n16_bit_adder_9_s4, n16_bit_adder_9_s5, n16_bit_adder_9_s6, n16_bit_adder_9_s7, n16_bit_adder_9_s8,
       n16_bit_adder_9_s9, n16_bit_adder_9_s10, n16_bit_adder_9_s11, n16_bit_adder_9_s12,
       n16_bit_adder_9_s13, n16_bit_adder_9_s14, n16_bit_adder_9_s15, n16_bit_adder_10_cout,
       n16_bit_adder_10_s1, n16_bit_adder_10_s2, n16_bit_adder_10_s3, n16_bit_adder_10_s4,
       n16_bit_adder_10_s5, n16_bit_adder_10_s6, n16_bit_adder_10_s7, n16_bit_adder_10_s8,
       n16_bit_adder_10_s9, n16_bit_adder_10_s10, n16_bit_adder_10_s11, n16_bit_adder_10_s12,
       n16_bit_adder_10_s13, n16_bit_adder_10_s14, n16_bit_adder_10_s15, n16_bit_adder_11_cout,
       n16_bit_adder_11_s1, n16_bit_adder_11_s2, n16_bit_adder_11_s3, n16_bit_adder_11_s4,
       n16_bit_adder_11_s5, n16_bit_adder_11_s6, n16_bit_adder_11_s7, n16_bit_adder_11_s8,
       n16_bit_adder_11_s9, n16_bit_adder_11_s10, n16_bit_adder_11_s11, n16_bit_adder_11_s12,
       n16_bit_adder_11_s13, n16_bit_adder_11_s14, n16_bit_adder_11_s15, n16_bit_adder_12_cout,
       n16_bit_adder_12_s1, n16_bit_adder_12_s2, n16_bit_adder_12_s3, n16_bit_adder_12_s4,
       n16_bit_adder_12_s5, n16_bit_adder_12_s6, n16_bit_adder_12_s7, n16_bit_adder_12_s8,
       n16_bit_adder_12_s9, n16_bit_adder_12_s10, n16_bit_adder_12_s11, n16_bit_adder_12_s12,
       n16_bit_adder_12_s13, n16_bit_adder_12_s14, n16_bit_adder_12_s15, n16_bit_adder_13_cout,
       n16_bit_adder_13_s1, n16_bit_adder_13_s2, n16_bit_adder_13_s3, n16_bit_adder_13_s4,
       n16_bit_adder_13_s5, n16_bit_adder_13_s6, n16_bit_adder_13_s7, n16_bit_adder_13_s8,
       n16_bit_adder_13_s9, n16_bit_adder_13_s10, n16_bit_adder_13_s11, n16_bit_adder_13_s12,
       n16_bit_adder_13_s13, n16_bit_adder_13_s14, n16_bit_adder_13_s15, n16_bit_adder_14_cout,
       n16_bit_adder_14_s1, n16_bit_adder_14_s2, n16_bit_adder_14_s3, n16_bit_adder_14_s4,
       n16_bit_adder_14_s5, n16_bit_adder_14_s6, n16_bit_adder_14_s7, n16_bit_adder_14_s8,
       n16_bit_adder_14_s9, n16_bit_adder_14_s10, n16_bit_adder_14_s11, n16_bit_adder_14_s12,
       n16_bit_adder_14_s13, n16_bit_adder_14_s14, n16_bit_adder_14_s15;

  // Probe on A
  // Probe on B
  // Probe on Output
  and and_1 (Output[0], B[0], A[0]);
  and and_2 (and_2_out, B[1], A[0]);
  and and_3 (and_3_out, B[2], A[0]);
  and and_4 (and_4_out, B[3], A[0]);
  and and_5 (and_5_out, B[4], A[0]);
  and and_6 (and_6_out, B[5], A[0]);
  and and_7 (and_7_out, B[6], A[0]);
  and and_8 (and_8_out, B[7], A[0]);
  and and_9 (and_9_out, B[8], A[0]);
  and and_10 (and_10_out, B[9], A[0]);
  and and_11 (and_11_out, B[10], A[0]);
  and and_12 (and_12_out, B[11], A[0]);
  and and_13 (and_13_out, B[12], A[0]);
  and and_14 (and_14_out, B[13], A[0]);
  and and_15 (and_15_out, B[14], A[0]);
  and and_16 (and_16_out, B[15], A[0]);
  and and_17 (and_17_out, B[0], A[1]);
  and and_18 (and_18_out, B[1], A[1]);
  and and_19 (and_19_out, B[2], A[1]);
  and and_20 (and_20_out, B[3], A[1]);
  and and_21 (and_21_out, B[4], A[1]);
  and and_22 (and_22_out, B[5], A[1]);
  and and_23 (and_23_out, B[6], A[1]);
  and and_24 (and_24_out, B[7], A[1]);
  and and_25 (and_25_out, B[8], A[1]);
  and and_26 (and_26_out, B[9], A[1]);
  and and_27 (and_27_out, B[10], A[1]);
  and and_28 (and_28_out, B[11], A[1]);
  and and_29 (and_29_out, B[12], A[1]);
  and and_30 (and_30_out, B[13], A[1]);
  and and_31 (and_31_out, B[14], A[1]);
  and and_32 (and_32_out, B[15], A[1]);
  and and_33 (and_33_out, B[0], A[2]);
  and and_34 (and_34_out, B[1], A[2]);
  and and_35 (and_35_out, B[2], A[2]);
  and and_36 (and_36_out, B[3], A[2]);
  and and_37 (and_37_out, B[4], A[2]);
  and and_38 (and_38_out, B[5], A[2]);
  and and_39 (and_39_out, B[6], A[2]);
  and and_40 (and_40_out, B[7], A[2]);
  and and_41 (and_41_out, B[8], A[2]);
  and and_42 (and_42_out, B[9], A[2]);
  and and_43 (and_43_out, B[10], A[2]);
  and and_44 (and_44_out, B[11], A[2]);
  and and_45 (and_45_out, B[12], A[2]);
  and and_46 (and_46_out, B[13], A[2]);
  and and_47 (and_47_out, B[14], A[2]);
  and and_48 (and_48_out, B[15], A[2]);
  and and_49 (and_49_out, B[0], A[3]);
  and and_50 (and_50_out, B[1], A[3]);
  and and_51 (and_51_out, B[2], A[3]);
  and and_52 (and_52_out, B[3], A[3]);
  and and_53 (and_53_out, B[4], A[3]);
  and and_54 (and_54_out, B[5], A[3]);
  and and_55 (and_55_out, B[6], A[3]);
  and and_56 (and_56_out, B[7], A[3]);
  and and_57 (and_57_out, B[8], A[3]);
  and and_58 (and_58_out, B[9], A[3]);
  and and_59 (and_59_out, B[10], A[3]);
  and and_60 (and_60_out, B[11], A[3]);
  and and_61 (and_61_out, B[12], A[3]);
  and and_62 (and_62_out, B[13], A[3]);
  and and_63 (and_63_out, B[14], A[3]);
  and and_64 (and_64_out, B[15], A[3]);
  and and_65 (and_65_out, B[0], A[4]);
  and and_66 (and_66_out, B[1], A[4]);
  and and_67 (and_67_out, B[2], A[4]);
  and and_68 (and_68_out, B[3], A[4]);
  and and_69 (and_69_out, B[4], A[4]);
  and and_70 (and_70_out, B[5], A[4]);
  and and_71 (and_71_out, B[6], A[4]);
  and and_72 (and_72_out, B[7], A[4]);
  and and_73 (and_73_out, B[8], A[4]);
  and and_74 (and_74_out, B[9], A[4]);
  and and_75 (and_75_out, B[10], A[4]);
  and and_76 (and_76_out, B[11], A[4]);
  and and_77 (and_77_out, B[12], A[4]);
  and and_78 (and_78_out, B[13], A[4]);
  and and_79 (and_79_out, B[14], A[4]);
  and and_80 (and_80_out, B[15], A[4]);
  and and_81 (and_81_out, B[0], A[5]);
  and and_82 (and_82_out, B[1], A[5]);
  and and_83 (and_83_out, B[2], A[5]);
  and and_84 (and_84_out, B[3], A[5]);
  and and_85 (and_85_out, B[4], A[5]);
  and and_86 (and_86_out, B[5], A[5]);
  and and_87 (and_87_out, B[6], A[5]);
  and and_88 (and_88_out, B[7], A[5]);
  and and_89 (and_89_out, B[8], A[5]);
  and and_90 (and_90_out, B[9], A[5]);
  and and_91 (and_91_out, B[10], A[5]);
  and and_92 (and_92_out, B[11], A[5]);
  and and_93 (and_93_out, B[12], A[5]);
  and and_94 (and_94_out, B[13], A[5]);
  and and_95 (and_95_out, B[14], A[5]);
  and and_96 (and_96_out, B[15], A[5]);
  and and_97 (and_97_out, B[0], A[6]);
  and and_98 (and_98_out, B[1], A[6]);
  and and_99 (and_99_out, B[2], A[6]);
  and and_100 (and_100_out, B[3], A[6]);
  and and_101 (and_101_out, B[4], A[6]);
  and and_102 (and_102_out, B[5], A[6]);
  and and_103 (and_103_out, B[6], A[6]);
  and and_104 (and_104_out, B[7], A[6]);
  and and_105 (and_105_out, B[8], A[6]);
  and and_106 (and_106_out, B[9], A[6]);
  and and_107 (and_107_out, B[10], A[6]);
  and and_108 (and_108_out, B[11], A[6]);
  and and_109 (and_109_out, B[12], A[6]);
  and and_110 (and_110_out, B[13], A[6]);
  and and_111 (and_111_out, B[14], A[6]);
  and and_112 (and_112_out, B[15], A[6]);
  and and_113 (and_113_out, B[0], A[7]);
  and and_114 (and_114_out, B[1], A[7]);
  and and_115 (and_115_out, B[2], A[7]);
  and and_116 (and_116_out, B[3], A[7]);
  and and_117 (and_117_out, B[4], A[7]);
  and and_118 (and_118_out, B[5], A[7]);
  and and_119 (and_119_out, B[6], A[7]);
  and and_120 (and_120_out, B[7], A[7]);
  and and_121 (and_121_out, B[8], A[7]);
  and and_122 (and_122_out, B[9], A[7]);
  and and_123 (and_123_out, B[10], A[7]);
  and and_124 (and_124_out, B[11], A[7]);
  and and_125 (and_125_out, B[12], A[7]);
  and and_126 (and_126_out, B[13], A[7]);
  and and_127 (and_127_out, B[14], A[7]);
  and and_128 (and_128_out, B[15], A[7]);
  and and_129 (and_129_out, B[0], A[8]);
  and and_130 (and_130_out, B[1], A[8]);
  and and_131 (and_131_out, B[2], A[8]);
  and and_132 (and_132_out, B[3], A[8]);
  and and_133 (and_133_out, B[4], A[8]);
  and and_134 (and_134_out, B[5], A[8]);
  and and_135 (and_135_out, B[6], A[8]);
  and and_136 (and_136_out, B[7], A[8]);
  and and_137 (and_137_out, B[8], A[8]);
  and and_138 (and_138_out, B[9], A[8]);
  and and_139 (and_139_out, B[10], A[8]);
  and and_140 (and_140_out, B[11], A[8]);
  and and_141 (and_141_out, B[12], A[8]);
  and and_142 (and_142_out, B[13], A[8]);
  and and_143 (and_143_out, B[14], A[8]);
  and and_144 (and_144_out, B[15], A[8]);
  and and_145 (and_145_out, B[0], A[9]);
  and and_146 (and_146_out, B[1], A[9]);
  and and_147 (and_147_out, B[2], A[9]);
  and and_148 (and_148_out, B[3], A[9]);
  and and_149 (and_149_out, B[4], A[9]);
  and and_150 (and_150_out, B[5], A[9]);
  and and_151 (and_151_out, B[6], A[9]);
  and and_152 (and_152_out, B[7], A[9]);
  and and_153 (and_153_out, B[8], A[9]);
  and and_154 (and_154_out, B[9], A[9]);
  and and_155 (and_155_out, B[10], A[9]);
  and and_156 (and_156_out, B[11], A[9]);
  and and_157 (and_157_out, B[12], A[9]);
  and and_158 (and_158_out, B[13], A[9]);
  and and_159 (and_159_out, B[14], A[9]);
  and and_160 (and_160_out, B[15], A[9]);
  and and_161 (and_161_out, B[0], A[10]);
  and and_162 (and_162_out, B[1], A[10]);
  and and_163 (and_163_out, B[2], A[10]);
  and and_164 (and_164_out, B[3], A[10]);
  and and_165 (and_165_out, B[4], A[10]);
  and and_166 (and_166_out, B[5], A[10]);
  and and_167 (and_167_out, B[6], A[10]);
  and and_168 (and_168_out, B[7], A[10]);
  and and_169 (and_169_out, B[8], A[10]);
  and and_170 (and_170_out, B[9], A[10]);
  and and_171 (and_171_out, B[10], A[10]);
  and and_172 (and_172_out, B[11], A[10]);
  and and_173 (and_173_out, B[12], A[10]);
  and and_174 (and_174_out, B[13], A[10]);
  and and_175 (and_175_out, B[14], A[10]);
  and and_176 (and_176_out, B[15], A[10]);
  and and_177 (and_177_out, B[0], A[11]);
  and and_178 (and_178_out, B[1], A[11]);
  and and_179 (and_179_out, B[2], A[11]);
  and and_180 (and_180_out, B[3], A[11]);
  and and_181 (and_181_out, B[4], A[11]);
  and and_182 (and_182_out, B[5], A[11]);
  and and_183 (and_183_out, B[6], A[11]);
  and and_184 (and_184_out, B[7], A[11]);
  and and_185 (and_185_out, B[8], A[11]);
  and and_186 (and_186_out, B[9], A[11]);
  and and_187 (and_187_out, B[10], A[11]);
  and and_188 (and_188_out, B[11], A[11]);
  and and_189 (and_189_out, B[12], A[11]);
  and and_190 (and_190_out, B[13], A[11]);
  and and_191 (and_191_out, B[14], A[11]);
  and and_192 (and_192_out, B[15], A[11]);
  and and_193 (and_193_out, B[0], A[12]);
  and and_194 (and_194_out, B[1], A[12]);
  and and_195 (and_195_out, B[2], A[12]);
  and and_196 (and_196_out, B[3], A[12]);
  and and_197 (and_197_out, B[4], A[12]);
  and and_198 (and_198_out, B[5], A[12]);
  and and_199 (and_199_out, B[6], A[12]);
  and and_200 (and_200_out, B[7], A[12]);
  and and_201 (and_201_out, B[8], A[12]);
  and and_202 (and_202_out, B[9], A[12]);
  and and_203 (and_203_out, B[10], A[12]);
  and and_204 (and_204_out, B[11], A[12]);
  and and_205 (and_205_out, B[12], A[12]);
  and and_206 (and_206_out, B[13], A[12]);
  and and_207 (and_207_out, B[14], A[12]);
  and and_208 (and_208_out, B[15], A[12]);
  and and_209 (and_209_out, B[0], A[13]);
  and and_210 (and_210_out, B[1], A[13]);
  and and_211 (and_211_out, B[2], A[13]);
  and and_212 (and_212_out, B[3], A[13]);
  and and_213 (and_213_out, B[4], A[13]);
  and and_214 (and_214_out, B[5], A[13]);
  and and_215 (and_215_out, B[6], A[13]);
  and and_216 (and_216_out, B[7], A[13]);
  and and_217 (and_217_out, B[8], A[13]);
  and and_218 (and_218_out, B[9], A[13]);
  and and_219 (and_219_out, B[10], A[13]);
  and and_220 (and_220_out, B[11], A[13]);
  and and_221 (and_221_out, B[12], A[13]);
  and and_222 (and_222_out, B[13], A[13]);
  and and_223 (and_223_out, B[14], A[13]);
  and and_224 (and_224_out, B[15], A[13]);
  and and_225 (and_225_out, B[0], A[14]);
  and and_226 (and_226_out, B[1], A[14]);
  and and_227 (and_227_out, B[2], A[14]);
  and and_228 (and_228_out, B[3], A[14]);
  and and_229 (and_229_out, B[4], A[14]);
  and and_230 (and_230_out, B[5], A[14]);
  and and_231 (and_231_out, B[6], A[14]);
  and and_232 (and_232_out, B[7], A[14]);
  and and_233 (and_233_out, B[8], A[14]);
  and and_234 (and_234_out, B[9], A[14]);
  and and_235 (and_235_out, B[10], A[14]);
  and and_236 (and_236_out, B[11], A[14]);
  and and_237 (and_237_out, B[12], A[14]);
  and and_238 (and_238_out, B[13], A[14]);
  and and_239 (and_239_out, B[14], A[14]);
  and and_240 (and_240_out, B[15], A[14]);
  and and_241 (and_241_out, B[0], A[15]);
  and and_242 (and_242_out, B[1], A[15]);
  and and_243 (and_243_out, B[2], A[15]);
  and and_244 (and_244_out, B[3], A[15]);
  and and_245 (and_245_out, B[4], A[15]);
  and and_246 (and_246_out, B[5], A[15]);
  and and_247 (and_247_out, B[6], A[15]);
  and and_248 (and_248_out, B[7], A[15]);
  and and_249 (and_249_out, B[8], A[15]);
  and and_250 (and_250_out, B[9], A[15]);
  and and_251 (and_251_out, B[10], A[15]);
  and and_252 (and_252_out, B[11], A[15]);
  and and_253 (and_253_out, B[12], A[15]);
  and and_254 (and_254_out, B[13], A[15]);
  and and_255 (and_255_out, B[14], A[15]);
  and and_256 (and_256_out, B[15], A[15]);
  _16_bit_Adder u_16_bit_adder_1 (
    .A15(1'b0), .A14(and_16_out), .A13(and_15_out), .A12(and_14_out), .A11(and_13_out), .A10(and_12_out),
    .A9(and_11_out), .A8(and_10_out), .A7(and_9_out), .A6(and_8_out), .A5(and_7_out), .A4(and_6_out),
    .A3(and_5_out), .A2(and_4_out), .A1(and_3_out), .A0(and_2_out), .B15(and_32_out), .B14(and_31_out),
    .B13(and_30_out), .B12(and_29_out), .B11(and_28_out), .B10(and_27_out), .B9(and_26_out), .B8(and_25_out),
    .B7(and_24_out), .B6(and_23_out), .B5(and_22_out), .B4(and_21_out), .B3(and_20_out), .B2(and_19_out),
    .B1(and_18_out), .B0(and_17_out), .Cin(1'b0), .Cout(n16_bit_adder_1_cout), .S15(n16_bit_adder_1_s15),
    .S14(n16_bit_adder_1_s14), .S13(n16_bit_adder_1_s13), .S12(n16_bit_adder_1_s12),
    .S11(n16_bit_adder_1_s11), .S10(n16_bit_adder_1_s10), .S9(n16_bit_adder_1_s9), .S8(n16_bit_adder_1_s8),
    .S7(n16_bit_adder_1_s7), .S6(n16_bit_adder_1_s6), .S5(n16_bit_adder_1_s5), .S4(n16_bit_adder_1_s4),
    .S3(n16_bit_adder_1_s3), .S2(n16_bit_adder_1_s2), .S1(n16_bit_adder_1_s1), .S0(Output[1]));
  _16_bit_Adder u_16_bit_adder_2 (
    .A15(n16_bit_adder_1_cout), .A14(n16_bit_adder_1_s15), .A13(n16_bit_adder_1_s14),
    .A12(n16_bit_adder_1_s13), .A11(n16_bit_adder_1_s12), .A10(n16_bit_adder_1_s11),
    .A9(n16_bit_adder_1_s10), .A8(n16_bit_adder_1_s9), .A7(n16_bit_adder_1_s8), .A6(n16_bit_adder_1_s7),
    .A5(n16_bit_adder_1_s6), .A4(n16_bit_adder_1_s5), .A3(n16_bit_adder_1_s4), .A2(n16_bit_adder_1_s3),
    .A1(n16_bit_adder_1_s2), .A0(n16_bit_adder_1_s1), .B15(and_48_out), .B14(and_47_out), .B13(and_46_out),
    .B12(and_45_out), .B11(and_44_out), .B10(and_43_out), .B9(and_42_out), .B8(and_41_out), .B7(and_40_out),
    .B6(and_39_out), .B5(and_38_out), .B4(and_37_out), .B3(and_36_out), .B2(and_35_out), .B1(and_34_out),
    .B0(and_33_out), .Cin(1'b0), .Cout(n16_bit_adder_2_cout), .S15(n16_bit_adder_2_s15),
    .S14(n16_bit_adder_2_s14), .S13(n16_bit_adder_2_s13), .S12(n16_bit_adder_2_s12),
    .S11(n16_bit_adder_2_s11), .S10(n16_bit_adder_2_s10), .S9(n16_bit_adder_2_s9), .S8(n16_bit_adder_2_s8),
    .S7(n16_bit_adder_2_s7), .S6(n16_bit_adder_2_s6), .S5(n16_bit_adder_2_s5), .S4(n16_bit_adder_2_s4),
    .S3(n16_bit_adder_2_s3), .S2(n16_bit_adder_2_s2), .S1(n16_bit_adder_2_s1), .S0(Output[2]));
  _16_bit_Adder u_16_bit_adder_3 (
    .A15(n16_bit_adder_2_cout), .A14(n16_bit_adder_2_s15), .A13(n16_bit_adder_2_s14),
    .A12(n16_bit_adder_2_s13), .A11(n16_bit_adder_2_s12), .A10(n16_bit_adder_2_s11),
    .A9(n16_bit_adder_2_s10), .A8(n16_bit_adder_2_s9), .A7(n16_bit_adder_2_s8), .A6(n16_bit_adder_2_s7),
    .A5(n16_bit_adder_2_s6), .A4(n16_bit_adder_2_s5), .A3(n16_bit_adder_2_s4), .A2(n16_bit_adder_2_s3),
    .A1(n16_bit_adder_2_s2), .A0(n16_bit_adder_2_s1), .B15(and_64_out), .B14(and_63_out), .B13(and_62_out),
    .B12(and_61_out), .B11(and_60_out), .B10(and_59_out), .B9(and_58_out), .B8(and_57_out), .B7(and_56_out),
    .B6(and_55_out), .B5(and_54_out), .B4(and_53_out), .B3(and_52_out), .B2(and_51_out), .B1(and_50_out),
    .B0(and_49_out), .Cin(1'b0), .Cout(n16_bit_adder_3_cout), .S15(n16_bit_adder_3_s15),
    .S14(n16_bit_adder_3_s14), .S13(n16_bit_adder_3_s13), .S12(n16_bit_adder_3_s12),
    .S11(n16_bit_adder_3_s11), .S10(n16_bit_adder_3_s10), .S9(n16_bit_adder_3_s9), .S8(n16_bit_adder_3_s8),
    .S7(n16_bit_adder_3_s7), .S6(n16_bit_adder_3_s6), .S5(n16_bit_adder_3_s5), .S4(n16_bit_adder_3_s4),
    .S3(n16_bit_adder_3_s3), .S2(n16_bit_adder_3_s2), .S1(n16_bit_adder_3_s1), .S0(Output[3]));
  _16_bit_Adder u_16_bit_adder_4 (
    .A15(n16_bit_adder_3_cout), .A14(n16_bit_adder_3_s15), .A13(n16_bit_adder_3_s14),
    .A12(n16_bit_adder_3_s13), .A11(n16_bit_adder_3_s12), .A10(n16_bit_adder_3_s11),
    .A9(n16_bit_adder_3_s10), .A8(n16_bit_adder_3_s9), .A7(n16_bit_adder_3_s8), .A6(n16_bit_adder_3_s7),
    .A5(n16_bit_adder_3_s6), .A4(n16_bit_adder_3_s5), .A3(n16_bit_adder_3_s4), .A2(n16_bit_adder_3_s3),
    .A1(n16_bit_adder_3_s2), .A0(n16_bit_adder_3_s1), .B15(and_80_out), .B14(and_79_out), .B13(and_78_out),
    .B12(and_77_out), .B11(and_76_out), .B10(and_75_out), .B9(and_74_out), .B8(and_73_out), .B7(and_72_out),
    .B6(and_71_out), .B5(and_70_out), .B4(and_69_out), .B3(and_68_out), .B2(and_67_out), .B1(and_66_out),
    .B0(and_65_out), .Cin(1'b0), .Cout(n16_bit_adder_4_cout), .S15(n16_bit_adder_4_s15),
    .S14(n16_bit_adder_4_s14), .S13(n16_bit_adder_4_s13), .S12(n16_bit_adder_4_s12),
    .S11(n16_bit_adder_4_s11), .S10(n16_bit_adder_4_s10), .S9(n16_bit_adder_4_s9), .S8(n16_bit_adder_4_s8),
    .S7(n16_bit_adder_4_s7), .S6(n16_bit_adder_4_s6), .S5(n16_bit_adder_4_s5), .S4(n16_bit_adder_4_s4),
    .S3(n16_bit_adder_4_s3), .S2(n16_bit_adder_4_s2), .S1(n16_bit_adder_4_s1), .S0(Output[4]));
  _16_bit_Adder u_16_bit_adder_5 (
    .A15(n16_bit_adder_4_cout), .A14(n16_bit_adder_4_s15), .A13(n16_bit_adder_4_s14),
    .A12(n16_bit_adder_4_s13), .A11(n16_bit_adder_4_s12), .A10(n16_bit_adder_4_s11),
    .A9(n16_bit_adder_4_s10), .A8(n16_bit_adder_4_s9), .A7(n16_bit_adder_4_s8), .A6(n16_bit_adder_4_s7),
    .A5(n16_bit_adder_4_s6), .A4(n16_bit_adder_4_s5), .A3(n16_bit_adder_4_s4), .A2(n16_bit_adder_4_s3),
    .A1(n16_bit_adder_4_s2), .A0(n16_bit_adder_4_s1), .B15(and_96_out), .B14(and_95_out), .B13(and_94_out),
    .B12(and_93_out), .B11(and_92_out), .B10(and_91_out), .B9(and_90_out), .B8(and_89_out), .B7(and_88_out),
    .B6(and_87_out), .B5(and_86_out), .B4(and_85_out), .B3(and_84_out), .B2(and_83_out), .B1(and_82_out),
    .B0(and_81_out), .Cin(1'b0), .Cout(n16_bit_adder_5_cout), .S15(n16_bit_adder_5_s15),
    .S14(n16_bit_adder_5_s14), .S13(n16_bit_adder_5_s13), .S12(n16_bit_adder_5_s12),
    .S11(n16_bit_adder_5_s11), .S10(n16_bit_adder_5_s10), .S9(n16_bit_adder_5_s9), .S8(n16_bit_adder_5_s8),
    .S7(n16_bit_adder_5_s7), .S6(n16_bit_adder_5_s6), .S5(n16_bit_adder_5_s5), .S4(n16_bit_adder_5_s4),
    .S3(n16_bit_adder_5_s3), .S2(n16_bit_adder_5_s2), .S1(n16_bit_adder_5_s1), .S0(Output[5]));
  _16_bit_Adder u_16_bit_adder_6 (
    .A15(n16_bit_adder_5_cout), .A14(n16_bit_adder_5_s15), .A13(n16_bit_adder_5_s14),
    .A12(n16_bit_adder_5_s13), .A11(n16_bit_adder_5_s12), .A10(n16_bit_adder_5_s11),
    .A9(n16_bit_adder_5_s10), .A8(n16_bit_adder_5_s9), .A7(n16_bit_adder_5_s8), .A6(n16_bit_adder_5_s7),
    .A5(n16_bit_adder_5_s6), .A4(n16_bit_adder_5_s5), .A3(n16_bit_adder_5_s4), .A2(n16_bit_adder_5_s3),
    .A1(n16_bit_adder_5_s2), .A0(n16_bit_adder_5_s1), .B15(and_112_out), .B14(and_111_out),
    .B13(and_110_out), .B12(and_109_out), .B11(and_108_out), .B10(and_107_out), .B9(and_106_out),
    .B8(and_105_out), .B7(and_104_out), .B6(and_103_out), .B5(and_102_out), .B4(and_101_out),
    .B3(and_100_out), .B2(and_99_out), .B1(and_98_out), .B0(and_97_out), .Cin(1'b0),
    .Cout(n16_bit_adder_6_cout), .S15(n16_bit_adder_6_s15), .S14(n16_bit_adder_6_s14),
    .S13(n16_bit_adder_6_s13), .S12(n16_bit_adder_6_s12), .S11(n16_bit_adder_6_s11),
    .S10(n16_bit_adder_6_s10), .S9(n16_bit_adder_6_s9), .S8(n16_bit_adder_6_s8), .S7(n16_bit_adder_6_s7),
    .S6(n16_bit_adder_6_s6), .S5(n16_bit_adder_6_s5), .S4(n16_bit_adder_6_s4), .S3(n16_bit_adder_6_s3),
    .S2(n16_bit_adder_6_s2), .S1(n16_bit_adder_6_s1), .S0(Output[6]));
  _16_bit_Adder u_16_bit_adder_7 (
    .A15(n16_bit_adder_6_cout), .A14(n16_bit_adder_6_s15), .A13(n16_bit_adder_6_s14),
    .A12(n16_bit_adder_6_s13), .A11(n16_bit_adder_6_s12), .A10(n16_bit_adder_6_s11),
    .A9(n16_bit_adder_6_s10), .A8(n16_bit_adder_6_s9), .A7(n16_bit_adder_6_s8), .A6(n16_bit_adder_6_s7),
    .A5(n16_bit_adder_6_s6), .A4(n16_bit_adder_6_s5), .A3(n16_bit_adder_6_s4), .A2(n16_bit_adder_6_s3),
    .A1(n16_bit_adder_6_s2), .A0(n16_bit_adder_6_s1), .B15(and_128_out), .B14(and_127_out),
    .B13(and_126_out), .B12(and_125_out), .B11(and_124_out), .B10(and_123_out), .B9(and_122_out),
    .B8(and_121_out), .B7(and_120_out), .B6(and_119_out), .B5(and_118_out), .B4(and_117_out),
    .B3(and_116_out), .B2(and_115_out), .B1(and_114_out), .B0(and_113_out), .Cin(1'b0),
    .Cout(n16_bit_adder_7_cout), .S15(n16_bit_adder_7_s15), .S14(n16_bit_adder_7_s14),
    .S13(n16_bit_adder_7_s13), .S12(n16_bit_adder_7_s12), .S11(n16_bit_adder_7_s11),
    .S10(n16_bit_adder_7_s10), .S9(n16_bit_adder_7_s9), .S8(n16_bit_adder_7_s8), .S7(n16_bit_adder_7_s7),
    .S6(n16_bit_adder_7_s6), .S5(n16_bit_adder_7_s5), .S4(n16_bit_adder_7_s4), .S3(n16_bit_adder_7_s3),
    .S2(n16_bit_adder_7_s2), .S1(n16_bit_adder_7_s1), .S0(Output[7]));
  _16_bit_Adder u_16_bit_adder_8 (
    .A15(n16_bit_adder_7_cout), .A14(n16_bit_adder_7_s15), .A13(n16_bit_adder_7_s14),
    .A12(n16_bit_adder_7_s13), .A11(n16_bit_adder_7_s12), .A10(n16_bit_adder_7_s11),
    .A9(n16_bit_adder_7_s10), .A8(n16_bit_adder_7_s9), .A7(n16_bit_adder_7_s8), .A6(n16_bit_adder_7_s7),
    .A5(n16_bit_adder_7_s6), .A4(n16_bit_adder_7_s5), .A3(n16_bit_adder_7_s4), .A2(n16_bit_adder_7_s3),
    .A1(n16_bit_adder_7_s2), .A0(n16_bit_adder_7_s1), .B15(and_144_out), .B14(and_143_out),
    .B13(and_142_out), .B12(and_141_out), .B11(and_140_out), .B10(and_139_out), .B9(and_138_out),
    .B8(and_137_out), .B7(and_136_out), .B6(and_135_out), .B5(and_134_out), .B4(and_133_out),
    .B3(and_132_out), .B2(and_131_out), .B1(and_130_out), .B0(and_129_out), .Cin(1'b0),
    .Cout(n16_bit_adder_8_cout), .S15(n16_bit_adder_8_s15), .S14(n16_bit_adder_8_s14),
    .S13(n16_bit_adder_8_s13), .S12(n16_bit_adder_8_s12), .S11(n16_bit_adder_8_s11),
    .S10(n16_bit_adder_8_s10), .S9(n16_bit_adder_8_s9), .S8(n16_bit_adder_8_s8), .S7(n16_bit_adder_8_s7),
    .S6(n16_bit_adder_8_s6), .S5(n16_bit_adder_8_s5), .S4(n16_bit_adder_8_s4), .S3(n16_bit_adder_8_s3),
    .S2(n16_bit_adder_8_s2), .S1(n16_bit_adder_8_s1), .S0(Output[8]));
  _16_bit_Adder u_16_bit_adder_9 (
    .A15(n16_bit_adder_8_cout), .A14(n16_bit_adder_8_s15), .A13(n16_bit_adder_8_s14),
    .A12(n16_bit_adder_8_s13), .A11(n16_bit_adder_8_s12), .A10(n16_bit_adder_8_s11),
    .A9(n16_bit_adder_8_s10), .A8(n16_bit_adder_8_s9), .A7(n16_bit_adder_8_s8), .A6(n16_bit_adder_8_s7),
    .A5(n16_bit_adder_8_s6), .A4(n16_bit_adder_8_s5), .A3(n16_bit_adder_8_s4), .A2(n16_bit_adder_8_s3),
    .A1(n16_bit_adder_8_s2), .A0(n16_bit_adder_8_s1), .B15(and_160_out), .B14(and_159_out),
    .B13(and_158_out), .B12(and_157_out), .B11(and_156_out), .B10(and_155_out), .B9(and_154_out),
    .B8(and_153_out), .B7(and_152_out), .B6(and_151_out), .B5(and_150_out), .B4(and_149_out),
    .B3(and_148_out), .B2(and_147_out), .B1(and_146_out), .B0(and_145_out), .Cin(1'b0),
    .Cout(n16_bit_adder_9_cout), .S15(n16_bit_adder_9_s15), .S14(n16_bit_adder_9_s14),
    .S13(n16_bit_adder_9_s13), .S12(n16_bit_adder_9_s12), .S11(n16_bit_adder_9_s11),
    .S10(n16_bit_adder_9_s10), .S9(n16_bit_adder_9_s9), .S8(n16_bit_adder_9_s8), .S7(n16_bit_adder_9_s7),
    .S6(n16_bit_adder_9_s6), .S5(n16_bit_adder_9_s5), .S4(n16_bit_adder_9_s4), .S3(n16_bit_adder_9_s3),
    .S2(n16_bit_adder_9_s2), .S1(n16_bit_adder_9_s1), .S0(Output[9]));
  _16_bit_Adder u_16_bit_adder_10 (
    .A15(n16_bit_adder_9_cout), .A14(n16_bit_adder_9_s15), .A13(n16_bit_adder_9_s14),
    .A12(n16_bit_adder_9_s13), .A11(n16_bit_adder_9_s12), .A10(n16_bit_adder_9_s11),
    .A9(n16_bit_adder_9_s10), .A8(n16_bit_adder_9_s9), .A7(n16_bit_adder_9_s8), .A6(n16_bit_adder_9_s7),
    .A5(n16_bit_adder_9_s6), .A4(n16_bit_adder_9_s5), .A3(n16_bit_adder_9_s4), .A2(n16_bit_adder_9_s3),
    .A1(n16_bit_adder_9_s2), .A0(n16_bit_adder_9_s1), .B15(and_176_out), .B14(and_175_out),
    .B13(and_174_out), .B12(and_173_out), .B11(and_172_out), .B10(and_171_out), .B9(and_170_out),
    .B8(and_169_out), .B7(and_168_out), .B6(and_167_out), .B5(and_166_out), .B4(and_165_out),
    .B3(and_164_out), .B2(and_163_out), .B1(and_162_out), .B0(and_161_out), .Cin(1'b0),
    .Cout(n16_bit_adder_10_cout), .S15(n16_bit_adder_10_s15), .S14(n16_bit_adder_10_s14),
    .S13(n16_bit_adder_10_s13), .S12(n16_bit_adder_10_s12), .S11(n16_bit_adder_10_s11),
    .S10(n16_bit_adder_10_s10), .S9(n16_bit_adder_10_s9), .S8(n16_bit_adder_10_s8), .S7(n16_bit_adder_10_s7),
    .S6(n16_bit_adder_10_s6), .S5(n16_bit_adder_10_s5), .S4(n16_bit_adder_10_s4), .S3(n16_bit_adder_10_s3),
    .S2(n16_bit_adder_10_s2), .S1(n16_bit_adder_10_s1), .S0(Output[10]));
  _16_bit_Adder u_16_bit_adder_11 (
    .A15(n16_bit_adder_10_cout), .A14(n16_bit_adder_10_s15), .A13(n16_bit_adder_10_s14),
    .A12(n16_bit_adder_10_s13), .A11(n16_bit_adder_10_s12), .A10(n16_bit_adder_10_s11),
    .A9(n16_bit_adder_10_s10), .A8(n16_bit_adder_10_s9), .A7(n16_bit_adder_10_s8), .A6(n16_bit_adder_10_s7),
    .A5(n16_bit_adder_10_s6), .A4(n16_bit_adder_10_s5), .A3(n16_bit_adder_10_s4), .A2(n16_bit_adder_10_s3),
    .A1(n16_bit_adder_10_s2), .A0(n16_bit_adder_10_s1), .B15(and_192_out), .B14(and_191_out),
    .B13(and_190_out), .B12(and_189_out), .B11(and_188_out), .B10(and_187_out), .B9(and_186_out),
    .B8(and_185_out), .B7(and_184_out), .B6(and_183_out), .B5(and_182_out), .B4(and_181_out),
    .B3(and_180_out), .B2(and_179_out), .B1(and_178_out), .B0(and_177_out), .Cin(1'b0),
    .Cout(n16_bit_adder_11_cout), .S15(n16_bit_adder_11_s15), .S14(n16_bit_adder_11_s14),
    .S13(n16_bit_adder_11_s13), .S12(n16_bit_adder_11_s12), .S11(n16_bit_adder_11_s11),
    .S10(n16_bit_adder_11_s10), .S9(n16_bit_adder_11_s9), .S8(n16_bit_adder_11_s8), .S7(n16_bit_adder_11_s7),
    .S6(n16_bit_adder_11_s6), .S5(n16_bit_adder_11_s5), .S4(n16_bit_adder_11_s4), .S3(n16_bit_adder_11_s3),
    .S2(n16_bit_adder_11_s2), .S1(n16_bit_adder_11_s1), .S0(Output[11]));
  _16_bit_Adder u_16_bit_adder_12 (
    .A15(n16_bit_adder_11_cout), .A14(n16_bit_adder_11_s15), .A13(n16_bit_adder_11_s14),
    .A12(n16_bit_adder_11_s13), .A11(n16_bit_adder_11_s12), .A10(n16_bit_adder_11_s11),
    .A9(n16_bit_adder_11_s10), .A8(n16_bit_adder_11_s9), .A7(n16_bit_adder_11_s8), .A6(n16_bit_adder_11_s7),
    .A5(n16_bit_adder_11_s6), .A4(n16_bit_adder_11_s5), .A3(n16_bit_adder_11_s4), .A2(n16_bit_adder_11_s3),
    .A1(n16_bit_adder_11_s2), .A0(n16_bit_adder_11_s1), .B15(and_208_out), .B14(and_207_out),
    .B13(and_206_out), .B12(and_205_out), .B11(and_204_out), .B10(and_203_out), .B9(and_202_out),
    .B8(and_201_out), .B7(and_200_out), .B6(and_199_out), .B5(and_198_out), .B4(and_197_out),
    .B3(and_196_out), .B2(and_195_out), .B1(and_194_out), .B0(and_193_out), .Cin(1'b0),
    .Cout(n16_bit_adder_12_cout), .S15(n16_bit_adder_12_s15), .S14(n16_bit_adder_12_s14),
    .S13(n16_bit_adder_12_s13), .S12(n16_bit_adder_12_s12), .S11(n16_bit_adder_12_s11),
    .S10(n16_bit_adder_12_s10), .S9(n16_bit_adder_12_s9), .S8(n16_bit_adder_12_s8), .S7(n16_bit_adder_12_s7),
    .S6(n16_bit_adder_12_s6), .S5(n16_bit_adder_12_s5), .S4(n16_bit_adder_12_s4), .S3(n16_bit_adder_12_s3),
    .S2(n16_bit_adder_12_s2), .S1(n16_bit_adder_12_s1), .S0(Output[12]));
  _16_bit_Adder u_16_bit_adder_13 (
    .A15(n16_bit_adder_12_cout), .A14(n16_bit_adder_12_s15), .A13(n16_bit_adder_12_s14),
    .A12(n16_bit_adder_12_s13), .A11(n16_bit_adder_12_s12), .A10(n16_bit_adder_12_s11),
    .A9(n16_bit_adder_12_s10), .A8(n16_bit_adder_12_s9), .A7(n16_bit_adder_12_s8), .A6(n16_bit_adder_12_s7),
    .A5(n16_bit_adder_12_s6), .A4(n16_bit_adder_12_s5), .A3(n16_bit_adder_12_s4), .A2(n16_bit_adder_12_s3),
    .A1(n16_bit_adder_12_s2), .A0(n16_bit_adder_12_s1), .B15(and_224_out), .B14(and_223_out),
    .B13(and_222_out), .B12(and_221_out), .B11(and_220_out), .B10(and_219_out), .B9(and_218_out),
    .B8(and_217_out), .B7(and_216_out), .B6(and_215_out), .B5(and_214_out), .B4(and_213_out),
    .B3(and_212_out), .B2(and_211_out), .B1(and_210_out), .B0(and_209_out), .Cin(1'b0),
    .Cout(n16_bit_adder_13_cout), .S15(n16_bit_adder_13_s15), .S14(n16_bit_adder_13_s14),
    .S13(n16_bit_adder_13_s13), .S12(n16_bit_adder_13_s12), .S11(n16_bit_adder_13_s11),
    .S10(n16_bit_adder_13_s10), .S9(n16_bit_adder_13_s9), .S8(n16_bit_adder_13_s8), .S7(n16_bit_adder_13_s7),
    .S6(n16_bit_adder_13_s6), .S5(n16_bit_adder_13_s5), .S4(n16_bit_adder_13_s4), .S3(n16_bit_adder_13_s3),
    .S2(n16_bit_adder_13_s2), .S1(n16_bit_adder_13_s1), .S0(Output[13]));
  _16_bit_Adder u_16_bit_adder_14 (
    .A15(n16_bit_adder_13_cout), .A14(n16_bit_adder_13_s15), .A13(n16_bit_adder_13_s14),
    .A12(n16_bit_adder_13_s13), .A11(n16_bit_adder_13_s12), .A10(n16_bit_adder_13_s11),
    .A9(n16_bit_adder_13_s10), .A8(n16_bit_adder_13_s9), .A7(n16_bit_adder_13_s8), .A6(n16_bit_adder_13_s7),
    .A5(n16_bit_adder_13_s6), .A4(n16_bit_adder_13_s5), .A3(n16_bit_adder_13_s4), .A2(n16_bit_adder_13_s3),
    .A1(n16_bit_adder_13_s2), .A0(n16_bit_adder_13_s1), .B15(and_240_out), .B14(and_239_out),
    .B13(and_238_out), .B12(and_237_out), .B11(and_236_out), .B10(and_235_out), .B9(and_234_out),
    .B8(and_233_out), .B7(and_232_out), .B6(and_231_out), .B5(and_230_out), .B4(and_229_out),
    .B3(and_228_out), .B2(and_227_out), .B1(and_226_out), .B0(and_225_out), .Cin(1'b0),
    .Cout(n16_bit_adder_14_cout), .S15(n16_bit_adder_14_s15), .S14(n16_bit_adder_14_s14),
    .S13(n16_bit_adder_14_s13), .S12(n16_bit_adder_14_s12), .S11(n16_bit_adder_14_s11),
    .S10(n16_bit_adder_14_s10), .S9(n16_bit_adder_14_s9), .S8(n16_bit_adder_14_s8), .S7(n16_bit_adder_14_s7),
    .S6(n16_bit_adder_14_s6), .S5(n16_bit_adder_14_s5), .S4(n16_bit_adder_14_s4), .S3(n16_bit_adder_14_s3),
    .S2(n16_bit_adder_14_s2), .S1(n16_bit_adder_14_s1), .S0(Output[14]));
  _16_bit_Adder u_16_bit_adder_15 (
    .A15(n16_bit_adder_14_cout), .A14(n16_bit_adder_14_s15), .A13(n16_bit_adder_14_s14),
    .A12(n16_bit_adder_14_s13), .A11(n16_bit_adder_14_s12), .A10(n16_bit_adder_14_s11),
    .A9(n16_bit_adder_14_s10), .A8(n16_bit_adder_14_s9), .A7(n16_bit_adder_14_s8), .A6(n16_bit_adder_14_s7),
    .A5(n16_bit_adder_14_s6), .A4(n16_bit_adder_14_s5), .A3(n16_bit_adder_14_s4), .A2(n16_bit_adder_14_s3),
    .A1(n16_bit_adder_14_s2), .A0(n16_bit_adder_14_s1), .B15(and_256_out), .B14(and_255_out),
    .B13(and_254_out), .B12(and_253_out), .B11(and_252_out), .B10(and_251_out), .B9(and_250_out),
    .B8(and_249_out), .B7(and_248_out), .B6(and_247_out), .B5(and_246_out), .B4(and_245_out),
    .B3(and_244_out), .B2(and_243_out), .B1(and_242_out), .B0(and_241_out), .Cin(1'b0), .Cout(Output[31]),
    .S15(Output[30]), .S14(Output[29]), .S13(Output[28]), .S12(Output[27]), .S11(Output[26]),
    .S10(Output[25]), .S9(Output[24]), .S8(Output[23]), .S7(Output[22]), .S6(Output[21]), .S5(Output[20]),
    .S4(Output[19]), .S3(Output[18]), .S2(Output[17]), .S1(Output[16]), .S0(Output[15]));
endmodule

module ALU_Control (
  input  [1:0] ALUOp,
  input  [1:0] Function,
  output [2:0] out_3,
  output [1:0] out_4
);

  wire and_1_out, and_2_out, and_3_out, and_4_out, and_5_out, and_6_out, and_7_out, and_8_out, and_9_out,
       and_10_out, and_11_out, not_1_out, not_2_out, not_3_out, xor_1_out;

  xor xor_1 (xor_1_out, ALUOp[1], ALUOp[0]);
  and and_1 (and_1_out, ~ALUOp[1], ~Function[0]);  // AND_Gate
  and and_2 (and_2_out, ALUOp[0], ~Function[1]);  // AND_Gate
  not not_1 (not_1_out, Function[0]);
  and and_3 (and_3_out, ~ALUOp[1], ~Function[1]);  // AND_Gate
  not not_2 (not_2_out, ALUOp[1]);
  not not_3 (not_3_out, Function[1]);
  and and_4 (and_4_out, ~ALUOp[0], Function[0]);  // AND_Gate
  and and_5 (and_5_out, ~ALUOp[0], ~Function[1]);  // AND_Gate
  and and_6 (and_6_out, ~ALUOp[1], ~Function[0]);  // AND_Gate
  and and_7 (and_7_out, ~ALUOp[1], ALUOp[0]);  // AND_Gate
  and and_8 (and_8_out, ALUOp[0], ~Function[0]);  // AND_Gate
  and and_9 (and_9_out, ALUOp[1], ~ALUOp[0], Function[0]);  // AND_Gate
  and and_10 (and_10_out, ~Function[0], ~Function[1]);  // AND_Gate
  and and_11 (and_11_out, ALUOp[0], Function[1], Function[0]);
  or or_1 (out_3[0], xor_1_out, and_1_out, and_2_out);
  or or_2 (out_3[1], not_1_out, and_3_out, xor_1_out);
  or or_3 (out_3[2], not_2_out, not_3_out, and_4_out);
  or or_4 (out_4[0], and_5_out, and_6_out, and_7_out, and_8_out, and_9_out);
  or or_5 (out_4[1], and_6_out, and_10_out, and_7_out, and_11_out, and_9_out);
endmodule

module ALU (
  input  [2:0] ALU_operation,
  input  [1:0] MUX_instruction,
  input  [31:0] A,
  input  [31:0] B,
  input  Cin,
  input  [15:0] A_2,
  input  [15:0] B_2,
  output [31:0] Output,
  output Zero,
  output out_10
);

  wire [31:0] n16x16_multiplier_1_output, n32_bit_arithmetic_unit_1_output, n32_bit_lu_1_output;

  // Probe on A
  // Probe on A_2
  // Probe on B_2
  // Probe on B
  _16x16_Multiplier u_16x16_multiplier_1 (.Output(n16x16_multiplier_1_output), .A(A_2), .B(B_2));
  // Probe on ALU_operation
  _32_bit_LU u_32_bit_lu_1 (.Output(n32_bit_lu_1_output), .A(B), .B(A), .S1S0(ALU_operation));
  _32_bit_Arithmetic_Unit u_32_bit_arithmetic_unit_1 (
    .S2S1S0(ALU_operation), .Output(n32_bit_arithmetic_unit_1_output), .Cout(out_10), .A(A), .B(B), .Cin(Cin));
  // Probe on MUX_instruction
  Multiplexer #(.select(2), .width(32), .enable("false")) multiplexer_1 (
    .in0(n32_bit_lu_1_output), .in1(n32_bit_arithmetic_unit_1_output), .in2(n16x16_multiplier_1_output),
    .out(Output), .sel(MUX_instruction));  // open: in3
  // Probe on Output
  nor nor_1 (Zero, Output[0], Output[1], Output[2], Output[3], Output[4], Output[5], Output[6], Output[7], Output[8], Output[9], Output[10], Output[11], Output[12], Output[13], Output[14], Output[15], Output[16], Output[17], Output[18], Output[19], Output[20], Output[21], Output[22], Output[23], Output[24], Output[25], Output[26], Output[27], Output[28], Output[29], Output[30], Output[31]);
endmodule

module Register_File (
  input  Write_En,
  input  [4:0] RD,
  input  [4:0] RS,
  input  [31:0] Data,
  input  Clock,
  input  Reset,
  input  [4:0] RT,
  output [31:0] Data_1,
  output [31:0] Data_2
);

  wire demultiplexer_1_out0, demultiplexer_1_out1, demultiplexer_1_out2, demultiplexer_1_out3,
       demultiplexer_1_out4, demultiplexer_1_out5, demultiplexer_1_out6, demultiplexer_1_out7,
       demultiplexer_1_out8, demultiplexer_1_out9, demultiplexer_1_out10, demultiplexer_1_out11,
       demultiplexer_1_out12, demultiplexer_1_out13, demultiplexer_1_out14, demultiplexer_1_out15,
       demultiplexer_1_out16, demultiplexer_1_out17, demultiplexer_1_out18, demultiplexer_1_out19,
       demultiplexer_1_out20, demultiplexer_1_out21, demultiplexer_1_out22, demultiplexer_1_out23,
       demultiplexer_1_out24, demultiplexer_1_out25, demultiplexer_1_out26, demultiplexer_1_out27,
       demultiplexer_1_out28, demultiplexer_1_out29, demultiplexer_1_out30, demultiplexer_1_out31;
  wire [31:0] register_1_q, register_2_q, register_3_q, register_4_q, register_5_q, register_6_q,
       register_7_q, register_8_q, register_9_q, register_10_q, register_11_q, register_12_q, register_13_q,
       register_14_q, register_15_q, register_16_q, register_17_q, register_18_q, register_19_q,
       register_20_q, register_21_q, register_22_q, register_23_q, register_24_q, register_25_q,
       register_26_q, register_27_q, register_28_q, register_29_q, register_30_q, register_31_q,
       register_32_q;

  Demultiplexer #(.select(5), .enable("false")) demultiplexer_1 (
    .out0(demultiplexer_1_out0), .out1(demultiplexer_1_out1), .out2(demultiplexer_1_out2),
    .out3(demultiplexer_1_out3), .out4(demultiplexer_1_out4), .out5(demultiplexer_1_out5),
    .out6(demultiplexer_1_out6), .out7(demultiplexer_1_out7), .out8(demultiplexer_1_out8),
    .out9(demultiplexer_1_out9), .out10(demultiplexer_1_out10), .out11(demultiplexer_1_out11),
    .out12(demultiplexer_1_out12), .out13(demultiplexer_1_out13), .out14(demultiplexer_1_out14),
    .out15(demultiplexer_1_out15), .out16(demultiplexer_1_out16), .out17(demultiplexer_1_out17),
    .out18(demultiplexer_1_out18), .out19(demultiplexer_1_out19), .out20(demultiplexer_1_out20),
    .out21(demultiplexer_1_out21), .out22(demultiplexer_1_out22), .out23(demultiplexer_1_out23),
    .out24(demultiplexer_1_out24), .out25(demultiplexer_1_out25), .out26(demultiplexer_1_out26),
    .out27(demultiplexer_1_out27), .out28(demultiplexer_1_out28), .out29(demultiplexer_1_out29),
    .out30(demultiplexer_1_out30), .out31(demultiplexer_1_out31), .in(Write_En), .sel(RD));
  Register #(.width(32)) register_1 (.D(Data), .en(demultiplexer_1_out0), .Q(register_1_q), .clk(Clock), .clr(Reset));
  Register #(.width(32)) register_2 (.D(Data), .en(demultiplexer_1_out1), .Q(register_2_q), .clk(Clock), .clr(Reset));
  Register #(.width(32)) register_3 (.D(Data), .en(demultiplexer_1_out2), .Q(register_3_q), .clk(Clock), .clr(Reset));
  Register #(.width(32)) register_4 (.D(Data), .en(demultiplexer_1_out3), .Q(register_4_q), .clk(Clock), .clr(Reset));
  Register #(.width(32)) register_5 (.D(Data), .en(demultiplexer_1_out4), .Q(register_5_q), .clk(Clock), .clr(Reset));
  Register #(.width(32)) register_6 (.D(Data), .en(demultiplexer_1_out5), .Q(register_6_q), .clk(Clock), .clr(Reset));
  Register #(.width(32)) register_7 (.D(Data), .en(demultiplexer_1_out6), .Q(register_7_q), .clk(Clock), .clr(Reset));
  Register #(.width(32)) register_8 (.D(Data), .en(demultiplexer_1_out7), .Q(register_8_q), .clk(Clock), .clr(Reset));
  Register #(.width(32)) register_9 (.D(Data), .en(demultiplexer_1_out8), .Q(register_9_q), .clk(Clock), .clr(Reset));
  Register #(.width(32)) register_10 (.D(Data), .en(demultiplexer_1_out9), .Q(register_10_q), .clk(Clock), .clr(Reset));
  Register #(.width(32)) register_11 (
    .D(Data), .en(demultiplexer_1_out10), .Q(register_11_q), .clk(Clock), .clr(Reset));
  Register #(.width(32)) register_12 (
    .D(Data), .en(demultiplexer_1_out11), .Q(register_12_q), .clk(Clock), .clr(Reset));
  Register #(.width(32)) register_13 (
    .D(Data), .en(demultiplexer_1_out12), .Q(register_13_q), .clk(Clock), .clr(Reset));
  Register #(.width(32)) register_14 (
    .D(Data), .en(demultiplexer_1_out13), .Q(register_14_q), .clk(Clock), .clr(Reset));
  Register #(.width(32)) register_15 (
    .D(Data), .en(demultiplexer_1_out14), .Q(register_15_q), .clk(Clock), .clr(Reset));
  Register #(.width(32)) register_16 (
    .D(Data), .en(demultiplexer_1_out15), .Q(register_16_q), .clk(Clock), .clr(Reset));
  Register #(.width(32)) register_17 (
    .D(Data), .en(demultiplexer_1_out16), .Q(register_17_q), .clk(Clock), .clr(Reset));
  Register #(.width(32)) register_18 (
    .D(Data), .en(demultiplexer_1_out17), .Q(register_18_q), .clk(Clock), .clr(Reset));
  Register #(.width(32)) register_19 (
    .D(Data), .en(demultiplexer_1_out18), .Q(register_19_q), .clk(Clock), .clr(Reset));
  Register #(.width(32)) register_20 (
    .D(Data), .en(demultiplexer_1_out19), .Q(register_20_q), .clk(Clock), .clr(Reset));
  Register #(.width(32)) register_21 (
    .D(Data), .en(demultiplexer_1_out20), .Q(register_21_q), .clk(Clock), .clr(Reset));
  Register #(.width(32)) register_22 (
    .D(Data), .en(demultiplexer_1_out21), .Q(register_22_q), .clk(Clock), .clr(Reset));
  Register #(.width(32)) register_23 (
    .D(Data), .en(demultiplexer_1_out22), .Q(register_23_q), .clk(Clock), .clr(Reset));
  Register #(.width(32)) register_24 (
    .D(Data), .en(demultiplexer_1_out23), .Q(register_24_q), .clk(Clock), .clr(Reset));
  Register #(.width(32)) register_25 (
    .D(Data), .en(demultiplexer_1_out24), .Q(register_25_q), .clk(Clock), .clr(Reset));
  Register #(.width(32)) register_26 (
    .D(Data), .en(demultiplexer_1_out25), .Q(register_26_q), .clk(Clock), .clr(Reset));
  Register #(.width(32)) register_27 (
    .D(Data), .en(demultiplexer_1_out26), .Q(register_27_q), .clk(Clock), .clr(Reset));
  Register #(.width(32)) register_28 (
    .D(Data), .en(demultiplexer_1_out27), .Q(register_28_q), .clk(Clock), .clr(Reset));
  Register #(.width(32)) register_29 (
    .D(Data), .en(demultiplexer_1_out28), .Q(register_29_q), .clk(Clock), .clr(Reset));
  Register #(.width(32)) register_30 (
    .D(Data), .en(demultiplexer_1_out29), .Q(register_30_q), .clk(Clock), .clr(Reset));
  Register #(.width(32)) register_31 (
    .D(Data), .en(demultiplexer_1_out30), .Q(register_31_q), .clk(Clock), .clr(Reset));
  Register #(.width(32)) register_32 (
    .D(Data), .en(demultiplexer_1_out31), .Q(register_32_q), .clk(Clock), .clr(Reset));
  Multiplexer #(.select(5), .width(32), .enable("false")) multiplexer_1 (
    .in0(register_1_q), .in1(register_2_q), .in2(register_3_q), .in3(register_4_q), .in4(register_5_q),
    .in5(register_6_q), .in6(register_7_q), .in7(register_8_q), .in8(register_9_q), .in9(register_10_q),
    .in10(register_11_q), .in11(register_12_q), .in12(register_13_q), .in13(register_14_q),
    .in14(register_15_q), .in15(register_16_q), .in16(register_17_q), .in17(register_18_q),
    .in18(register_19_q), .in19(register_20_q), .in20(register_21_q), .in21(register_22_q),
    .in22(register_23_q), .in23(register_24_q), .in24(register_25_q), .in25(register_26_q),
    .in26(register_27_q), .in27(register_28_q), .in28(register_29_q), .in29(register_30_q),
    .in30(register_31_q), .in31(register_32_q), .out(Data_1), .sel(RS));
  Multiplexer #(.select(5), .width(32), .enable("false")) multiplexer_2 (
    .in0(register_1_q), .in1(register_2_q), .in2(register_3_q), .in3(register_4_q), .in4(register_5_q),
    .in5(register_6_q), .in6(register_7_q), .in7(register_8_q), .in8(register_9_q), .in9(register_10_q),
    .in10(register_11_q), .in11(register_12_q), .in12(register_13_q), .in13(register_14_q),
    .in14(register_15_q), .in15(register_16_q), .in16(register_17_q), .in17(register_18_q),
    .in18(register_19_q), .in19(register_20_q), .in20(register_21_q), .in21(register_22_q),
    .in22(register_23_q), .in23(register_24_q), .in24(register_25_q), .in25(register_26_q),
    .in26(register_27_q), .in27(register_28_q), .in28(register_29_q), .in29(register_30_q),
    .in30(register_31_q), .in31(register_32_q), .out(Data_2), .sel(RT));
endmodule

module Main_Control (
  input  [5:0] Opcode,
  output R_dest,
  output R_type___I_type,
  output ALU___Memory,
  output R_Write,
  output SW,
  output LW,
  output [1:0] ALUOp,
  output [1:0] Function,
  output Cin,
  output Brunch,
  output Jump
);

  wire and_1_out, and_2_out, and_3_out, and_4_out, and_5_out, and_6_out, and_7_out, and_8_out, and_9_out,
       not_1_out, not_2_out, not_3_out, not_4_out, not_5_out, not_6_out;

  not not_1 (not_1_out, Opcode[5]);
  not not_2 (not_2_out, Opcode[4]);
  not not_3 (not_3_out, Opcode[3]);
  not not_4 (not_4_out, Opcode[2]);
  not not_5 (not_5_out, Opcode[1]);
  not not_6 (not_6_out, Opcode[0]);
  and and_1 (and_1_out, not_1_out, not_2_out, not_3_out, not_4_out, Opcode[1], Opcode[0]);
  and and_2 (and_2_out, not_1_out, not_2_out, Opcode[3], not_4_out, not_5_out, not_6_out);
  and and_3 (and_3_out, not_1_out, not_2_out, not_3_out, Opcode[2], not_5_out, not_6_out);
  and and_4 (and_4_out, not_1_out, not_2_out, not_3_out, not_4_out, not_5_out, not_6_out);
  and and_5 (and_5_out, not_1_out, not_2_out, not_3_out, not_4_out, not_5_out, Opcode[0]);
  and and_6 (and_6_out, not_1_out, not_2_out, not_3_out, Opcode[2], Opcode[1], not_6_out);
  and and_7 (and_7_out, not_1_out, not_2_out, not_3_out, Opcode[2], Opcode[1], Opcode[0]);
  and and_8 (and_8_out, not_1_out, not_2_out, Opcode[3], not_4_out, Opcode[1], Opcode[0]);
  and and_9 (and_9_out, not_1_out, not_2_out, Opcode[3], Opcode[2], not_5_out, not_6_out);
  and and_10 (SW, not_1_out, not_2_out, Opcode[3], Opcode[2], not_5_out, Opcode[0]);
  and and_11 (ALU___Memory, not_1_out, not_2_out, Opcode[3], Opcode[2], Opcode[1], Opcode[0]);
  and and_12 (Brunch, not_1_out, not_2_out, Opcode[3], not_4_out, Opcode[1], not_6_out);
  and and_13 (Jump, not_1_out, not_2_out, Opcode[3], Opcode[2], Opcode[1], not_6_out);
  or or_1 (R_dest, and_1_out, and_2_out, and_3_out, Brunch, and_4_out, and_5_out, and_8_out);
  or or_2 (R_type___I_type, and_6_out, and_7_out, and_9_out, SW, ALU___Memory);
  or or_3 (R_Write, and_1_out, and_2_out, and_3_out, and_4_out, and_5_out, and_6_out, and_7_out, and_8_out, and_9_out, ALU___Memory);
  or or_4 (ALUOp[1], and_1_out, and_3_out, and_4_out, and_6_out, and_8_out, and_9_out, SW, ALU___Memory);
  or or_5 (ALUOp[0], and_3_out, and_4_out, and_6_out, and_8_out, and_9_out, SW, ALU___Memory);
  or or_6 (Function[1], and_1_out, and_2_out, and_4_out, and_6_out, and_8_out, and_9_out, SW, ALU___Memory);
  or or_7 (Function[0], and_2_out, and_3_out, and_5_out, Brunch, and_7_out, and_8_out, and_9_out);
  or or_8 (Cin, and_5_out, Brunch, and_7_out);

  assign LW = ALU___Memory;
endmodule

module Prosessor (
  input  Reset,
  input  [15:0] IMM___Offset,
  input  [5:0] Opcode,
  input  [4:0] RS,
  input  [4:0] RT,
  input  [4:0] RD,
  input  [4:0] SA,
  input  [5:0] Function,
  input  [5:0] Opcode_2,
  input  [4:0] RS_2,
  input  [4:0] RT_2,
  output [5:0] Opcode_3,
  output [4:0] RS_3,
  output [4:0] RT_3,
  output [4:0] RD_2,
  output [4:0] SA_2,
  output [15:0] Immediate,
  output [31:0] Output_of_Logical_Operation,
  output [5:0] Function_2,
  output Cout
);

  wire alu_1_zero, ALU___Memory, and_1_out, Branch, Cin, Clock, Jmp, LW, R_dest, R_type___I_type, R_write, SW;
  wire [1:0] ALUOp, Function_t, MUX_instruction;
  wire [2:0] ALU_operation;
  wire [4:0] multiplexer_1_out;
  wire [15:0] adder_1_out, multiplexer_4_out, register_1_q;
  wire [31:0] bit_extender_2_out, bit_extender_3_out, Data, Data_2, Increment, multiplexer_2_out,
       multiplexer_3_out, ram_1_data, register_file_1_data_1;
  wire [31:16] multiplexer_4_out_2;

  Register #(.width(16)) register_1 (.D(multiplexer_4_out), .Q(register_1_q), .clk(Clock), .clr(Reset));  // open: en
  Clock u_Clock (.out(Clock));
  Adder #(.width(16)) adder_1 (.a(register_1_q), .b(16'h1), .out(adder_1_out));  // open: cin, cout
  assign Increment = {{16{1'b0}}, adder_1_out};  // Bit_Extender bit_extender_1
  ROM #(.addrWidth(16), .dataWidth(32)) rom_1 (
    .addr(register_1_q), .data({Opcode_3, RS_3, RT_3, Immediate[15:6], Function_2}), .sel(1'b1));
  // Probe on Data
  // Probe on {Opcode, RS, RT, RD, SA, Function}
  Multiplexer #(.width(5), .enable("false")) multiplexer_1 (
    .in0(RT_3), .in1(Immediate[15:11]), .out(multiplexer_1_out), .sel(R_dest));
  assign bit_extender_2_out = {{16{1'b0}}, {Immediate[15:6], Function_2}};  // Bit_Extender bit_extender_2
  // Probe on {Immediate[15:6], Function_2}
  Register_File register_file_1 (
    .Write_En(R_write), .Data(Data), .Clock(Clock), .Reset(Reset), .Data_1(register_file_1_data_1),
    .RS(RS_3), .Data_2(Data_2), .RT(RT_3), .RD(multiplexer_1_out));
  // Probe on {Opcode_2, RS_2, RT_2, IMM___Offset}
  assign bit_extender_3_out = {{6{1'b0}}, {RS_3, RT_3, Immediate[15:6], Function_2}};  // Bit_Extender bit_extender_3
  Multiplexer #(.width(32), .enable("false")) multiplexer_2 (
    .in0(Data_2), .in1(bit_extender_2_out), .out(multiplexer_2_out), .sel(R_type___I_type));
  Multiplexer #(.width(32), .enable("false")) multiplexer_3 (
    .in0(Increment), .in1(bit_extender_2_out), .out(multiplexer_3_out), .sel(and_1_out));
  and and_1 (and_1_out, alu_1_zero, Branch);
  Multiplexer #(.width(32), .enable("false")) multiplexer_4 (
    .in0(multiplexer_3_out), .in1(bit_extender_3_out), .out({multiplexer_4_out_2, multiplexer_4_out}),
    .sel(Jmp));
  ALU alu_1 (
    .A(register_file_1_data_1), .B(multiplexer_2_out), .Cin(Cin), .A_2(register_file_1_data_1[15:0]),
    .B_2(multiplexer_2_out[15:0]), .Output(Output_of_Logical_Operation), .out_10(Cout), .Zero(alu_1_zero),
    .ALU_operation(ALU_operation), .MUX_instruction(MUX_instruction));
  Main_Control main_control_1 (
    .R_dest(R_dest), .R_type___I_type(R_type___I_type), .ALU___Memory(ALU___Memory), .R_Write(R_write),
    .SW(SW), .LW(LW), .ALUOp(ALUOp), .Function(Function_t), .Opcode(Opcode_3), .Cin(Cin), .Brunch(Branch),
    .Jump(Jmp));
  // Probe on Output_of_Logical_Operation
  Multiplexer #(.width(32), .enable("false")) multiplexer_5 (
    .in0(Output_of_Logical_Operation), .in1(ram_1_data), .out(Data), .sel(ALU___Memory));
  RAM #(.addrWidth(16), .dataWidth(32), .bus("separate")) ram_1 (
    .addr(Output_of_Logical_Operation[15:0]), .din(Data_2), .data(ram_1_data), .str(SW), .sel(1'b1),
    .clk(Clock), .ld(LW), .clr(Reset));
  ALU_Control alu_control_1 (.out_3(ALU_operation), .out_4(MUX_instruction), .ALUOp(ALUOp), .Function(Function_t));

  assign Immediate[5:0] = Function_2;
  assign RD_2 = Immediate[15:11];
  assign SA_2 = Immediate[10:6];

  // Other names for the same wires on the sheet: Opcode_t[5:0] = Opcode_3

  // Notes on the sheet:
  //   Instruction Memory
  //   contents of rom_1 (hex, n*v repeats v):
  //   3c220006
  //   R-format HEX converter
  //   Offset/
  //   I-format HEX converter
  //   32-bit MIPS
  //   Processor
  //   Data Memory
endmodule
